# Fritzing sketch 06_lab4_main3_1_diagram (saved by Fritzing 0.9.3b)
breadboards: 1

parts:
  J1 = STM32 Nucleo boards
  R1 = Resistor [tolerance=±5% resistance=220 package=THT]
  R3 = Resistor [tolerance=±5% resistance=220 package=THT]
  R4 = Resistor [tolerance=±5% resistance=220 package=THT]
  LED1 = LED - 5mm [color="Blue (430nm)" package="5 mm [THT]"]
  LED2 = LED - 5mm [color="Blue (430nm)" package="5 mm [THT]"]
  R5 = Resistor [tolerance=±5% resistance=220 package=THT]
  LED3 = LED - 5mm [color="Blue (430nm)" package="5 mm [THT]"]
  LED4 = LED - 5mm [color="Blue (430nm)" package="5 mm [THT]"]

nets:
  N1: J1.PB6, R1.Pin_1
  N2: J1.PB4, R3.Pin_1
  N3: J1.PB5, R5.Pin_1
  N4: J1.PB3, R4.Pin_1
  N5: R1.Pin_0, LED1.anode
  N6: R3.Pin_0, LED3.anode
  N7: R4.Pin_0, LED4.anode
  N8: LED1.cathode, LED2.cathode, LED3.cathode, LED4.cathode
  N9: LED2.anode, R5.Pin_0
